// Logisim project CPU Assembly 2026.circ as structural Verilog: 1 circuit, main circuit main
// Reset
module main (
  input  [7:0] in_1,
  input  in_2,
  input  load_a,
  input  en_a,
  input  load,
  input  sub,
  input  add,
  input  en_alu,
  input  ram_in,
  input  load_b,
  input  ram_out,
  input  en_b,
  input  in_13
);

  wire alu2025_1_cout, clock, clock_1_out, reset;
  wire [3:0] main_3__4bit_data_out;
  wire [7:0] alu2025_1_contents, main_2_bus, main_2_contents, main_3_contents, main_4_internal_content,
       main_5_internal_content;

  Clock clock_1 (.out(clock_1_out));
  Button u_reset (.out(reset));
  Clock_Module_main main_1 (.Clock_In(clock_1_out), .Halt(in_13), .Clock_Out(clock));
  ram_module_without_MAR_main main_2 (
    .data_in(main_2_bus), .oe(ram_out), .write(ram_in), .contents(main_2_contents), .bus(main_2_bus),
    .add_in(main_3__4bit_data_out), .clr(reset), .clk(clock));
  // Probe on main_2_bus
  assign main_2_bus = in_2 ? in_1 : 8'bz;  // Controlled_Buffer controlled_buffer_1
  // Probe on main_3_contents
  MAR_module_main main_3 (
    .load_in(load), .rst(reset), .clk(clock), .bus_datain(main_2_bus),
    ._4bit_data_out(main_3__4bit_data_out), .contents(main_3_contents));
  // Probe on main_2_contents
  _8bit_reg_module_74_based_main main_4 (
    .internal_content(main_4_internal_content), .datain(main_2_bus), .loadn(load_a), .clk(clock),
    .rst(reset), .oe(en_a), .bus(main_2_bus));
  // Probe on main_4_internal_content
  // Probe on alu2025_1_contents
  // Probe on main_5_internal_content
  _8bit_reg_module_74_based_main main_5 (
    .internal_content(main_5_internal_content), .datain(main_2_bus), .loadn(load_b), .clk(clock),
    .rst(reset), .oe(en_b), .bus(main_2_bus));
  // Probe on alu2025_1_cout
  ALU2025 alu2025_1 (
    .Cout(alu2025_1_cout), .OUTPUT(main_2_bus), .B(main_5_internal_content), .A(main_4_internal_content),
    .Sub_Cin(sub), .Add(add), .Mul(1'b0), .XOR(1'b0), .AND(1'b0), .OR(1'b0), .Bus_Enable(en_alu),
    .contents(alu2025_1_contents));
endmodule
